# Fritzing sketch electronic (saved by Fritzing 0.8.5b)
breadboards: 1

parts:
  R1 = Resistor [tolerance=±5% resistance=150 package=THT]
  C1 = Tantalum Capacitor [capacitance=22µF package="100 mil [THT, tantalum]"]
  Q1 = NPN-Transistor [package="TO92 [THT]"]
  R3 = Resistor [tolerance=±5% resistance=1k package=THT]
  R4 = Resistor [tolerance=±5% resistance=1k package=THT]
  R5 = Resistor [tolerance=±5% resistance=1k package=THT]
  R6 = Resistor [tolerance=±5% resistance=4.7k package=THT]
  R7 = Resistor [tolerance=±5% resistance=4.7k package=THT]
  R8 = Resistor [tolerance=±5% resistance=10k package=THT]
  C2 = Tantalum Capacitor [capacitance=1μF package="100 mil [THT, tantalum]"]
  R9 = Resistor [tolerance=±5% resistance=100 package=THT]

nets:
  5V/GPY pin6/MQ-7 H1: R1.Pin_0
  GPY pin1: R1.Pin_1, C1.+
  DHT11 pin4/DS18B20 pin1/GND/GPY pin2/GPY pin4/LPS331AP GND/MQ-7 H2/TSOP312 GND: C1.-, Q1.E, R5.Pin_1, R8.Pin_1, C2.-
  N1: Q1.B, R3.Pin_1
  GPY pin3: Q1.C
  GPIO ENABLE SAMPLING: R3.Pin_0
  GPY pin5: R4.Pin_0
  ANALOG IN (divided by 2): R4.Pin_1, R5.Pin_0
  3.3V/DHT11 pin1/DS18B20 pin3/LPS331AP VIN/MQ-7 A: R6.Pin_0, R7.Pin_1, R9.Pin_0
  DHT11 pin2/DIGITAL IN [DHT-11]: R6.Pin_1
  DS18B20 pin2/ONE WIRE [DS18B20]: R7.Pin_0
  ANALOG IN [MQ-7]/MQ-7 B: R8.Pin_0
  TSOP312 Vs: C2.+, R9.Pin_1
